# Fritzing sketch rascunho (saved by Fritzing 0.9.3b)
breadboards: 1

parts:
  Componente1 = Arduino Uno (Rev3)
  LED1 = smd LED [color="Red (633nm)" package="0805 [SMD]"]
  R2 = Resistor [tolerance=±5% resistance=220 package="0402 [SMD]"]
  S1 = Pushbutton [package="[SMD]"]
  R3 = Resistor [tolerance=±5% resistance=220 package="0603 [SMD]"]
  R4 = Resistor [tolerance=±5% resistance=220 package="0603 [SMD]"]
  R5 = Resistor [tolerance=±5% resistance=220 package="0603 [SMD]"]
  LED2 = smd LED [color="Yellow (585nm)" package="1206 [SMD]"]
  LED3 = smd LED [color="Green (555nm)" package="1206 [SMD]"]
  LED4 = smd LED [color="Blue (430nm)" package="1206 [SMD]"]
  S2 = Pushbutton [package="[SMD]"]
  S3 = Pushbutton [package="[SMD]"]
  S4 = Pushbutton [package="[SMD]"]
  U1 = POT [package=pot_alpha_rv16af-20]

nets:
  N1: Componente1.D8, S2.Pin_1, S2.Pin_2
  N2: Componente1.D9_PWM, S3.Pin_1, S3.Pin_2
  N3: Componente1.D10_PWM/SS, S1.Pin_1, S1.Pin_2
  N4: Componente1.D11_PWM/MOSI, S4.Pin_1, S4.Pin_2
  N5: Componente1.D2, LED3.anode
  N6: Componente1.D3_PWM, LED2.anode
  N7: Componente1.D4, LED1.anode
  N8: Componente1.D5_PWM, LED4.anode
  N9: Componente1.5V, U1.E
  N10: Componente1.GND, R2.Pin_1, S1.Pin_3, S1.Pin_4, R3.Pin_1, R4.Pin_1, R5.Pin_1, U1.A
  N11: LED1.cathode, R2.Pin_0
  N12: R3.Pin_0, LED4.cathode
  N13: R4.Pin_0, LED2.cathode
  N14: R5.Pin_0, LED3.cathode
  N15: S2.Pin_3, S2.Pin_4
  N16: S3.Pin_3, S3.Pin_4
  N17: S4.Pin_3, S4.Pin_4
